// Logisim project GTU-PingPongGame.circ as structural Verilog
module main (
  input  Go,
  input  Win
);

  wire and_1_out, and_2_out, and_3_out, and_4_out, and_5_out, and_6_out, and_7_out, and_8_out, and_9_out,
       and_10_out, and_11_out, and_12_out, and_13_out, and_14_out, and_15_out, and_16_out, and_17_out,
       and_19_out, and_20_out, and_21_out, and_22_out, and_23_out, and_24_out, and_25_out, and_26_out,
       and_27_out, and_28_out, and_29_out, and_31_out, and_32_out, and_34_out, and_36_out, and_37_out, by,
       byP1, byP2, clock_out, comparator_1_lt, comparator_3_eq, comparator_4_eq, comparator_5_lt,
       counter_2_q, counter_4_q, loop1, multiplexer_1_out, not_1_out, not_2_out, not_3_out, not_4_out,
       not_5_out, not_6_out, not_7_out, not_8_out, not_9_out, not_10_out, not_12_out, not_14_out, or_1_out,
       or_2_out, or_3_out, or_4_out, or_5_out, or_6_out, or_7_out, or_8_out, or_10_out, or_11_out, or_13_out,
       or_14_out, or_15_out, p2_prime_p1p0_prime, reset, score, scoreStop, state0, state1, state2, state2_3,
       state3, state4, state5, state6, state7, xBegin, xEnd, xor_1_out, xor_2_out, yBegin, yEnd;
  wire [2:0] d_ff_3_q;
  wire [3:0] countBall_Y_q, counter_1_q, counter_3_q, joystick_1_x, joystick_1_y, joystick_2_x, joystick_2_y;
  wire [4:0] countBall_X_q, register_1_q;
  wire [9:0] and_33_out, and_35_out, ball_Y_2_q, ball_Y_q, demultiplexer_1_out1, demultiplexer_1_out2,
       demultiplexer_1_out3, demultiplexer_1_out4, demultiplexer_1_out5, demultiplexer_1_out6,
       demultiplexer_1_out7, demultiplexer_1_out8, demultiplexer_1_out9, demultiplexer_1_out10,
       demultiplexer_1_out11, demultiplexer_1_out12, demultiplexer_1_out13, demultiplexer_1_out14,
       demultiplexer_1_out15, demultiplexer_1_out16, demultiplexer_1_out17, demultiplexer_1_out18,
       demultiplexer_1_out19, multiplexer_3_out, multiplexer_4_out, or_17_out, player1_1_outplayer1,
       player2_1_outplayer2, shifter_1_out, shifter_2_out;

  Button button_1 (.out(reset));
  not not_1 (not_1_out, d_ff_3_q[2]);
  not not_2 (not_2_out, d_ff_3_q[1]);
  not not_3 (not_3_out, d_ff_3_q[0]);
  not not_4 (not_4_out, d_ff_3_q[1]);
  not not_5 (not_5_out, d_ff_3_q[0]);
  and and_1 (and_1_out, ~d_ff_3_q[2], d_ff_3_q[1], d_ff_3_q[0]);  // AND_Gate
  and and_2 (and_2_out, d_ff_3_q[2], d_ff_3_q[1], ~d_ff_3_q[0], score);  // AND_Gate
  and and_3 (and_3_out, xEnd, ~loop1, byP2);  // AND_Gate
  not not_6 (not_6_out, d_ff_3_q[2]);
  and and_4 (and_4_out, xEnd, ~byP2);  // AND_Gate
  and and_5 (and_5_out, ~xEnd, ~xBegin, loop1);  // AND_Gate
  and and_6 (and_6_out, ~d_ff_3_q[2], ~d_ff_3_q[1], d_ff_3_q[0]);  // AND_Gate
  and and_7 (and_7_out, d_ff_3_q[2], ~d_ff_3_q[1], ~d_ff_3_q[0]);  // AND_Gate
  and and_8 (and_8_out, d_ff_3_q[2], ~d_ff_3_q[1], ~d_ff_3_q[0], byP2, loop1);  // AND_Gate
  and and_9 (and_9_out, d_ff_3_q[2], ~d_ff_3_q[1], ~d_ff_3_q[0], xEnd, ~loop1);  // AND_Gate
  and and_10 (and_10_out, ~d_ff_3_q[2], d_ff_3_q[1], d_ff_3_q[0], xBegin, loop1, ~byP1);  // AND_Gate
  and and_11 (and_11_out, d_ff_3_q[2], d_ff_3_q[1], d_ff_3_q[0], ~reset);  // AND_Gate
  and and_12 (and_12_out, ~d_ff_3_q[2], ~d_ff_3_q[1], ~d_ff_3_q[0], Go);  // AND_Gate
  and and_13 (and_13_out, xEnd, ~byP2);  // AND_Gate
  and and_14 (and_14_out, loop1, byP1, xBegin);
  and and_15 (and_15_out, ~xBegin, ~xEnd);  // AND_Gate
  not not_7 (not_7_out, d_ff_3_q[0]);
  and and_16 (and_16_out, ~byP1, byP2);  // AND_Gate
  or or_1 (or_1_out, and_16_out, and_17_out);
  and and_17 (and_17_out, ~byP2, byP1);  // AND_Gate
  and and_18 (p2_prime_p1p0_prime, not_1_out, not_3_out, d_ff_3_q[1]);
  or or_2 (or_2_out, score, and_3_out);
  and and_19 (and_19_out, or_2_out, p2_prime_p1p0_prime);
  and and_20 (and_20_out, xBegin, byP1, not_6_out, d_ff_3_q[1], d_ff_3_q[0], loop1);
  and and_21 (and_21_out, loop1, d_ff_3_q[2], not_4_out, not_5_out, xEnd, byP2);
  and and_22 (and_22_out, xEnd, byP2, not_10_out, not_9_out, d_ff_3_q[2]);
  and and_23 (and_23_out, d_ff_3_q[2], d_ff_3_q[1], d_ff_3_q[0], ~reset);  // AND_Gate
  or or_3 (or_3_out, and_4_out, and_5_out, score);
  and and_24 (and_24_out, or_3_out, p2_prime_p1p0_prime);
  and and_25 (and_25_out, and_7_out, byP1, ~byP2);  // AND_Gate
  and and_26 (and_26_out, ~xEnd, ~xBegin, ~d_ff_3_q[2], d_ff_3_q[1], d_ff_3_q[0]);  // AND_Gate
  and and_27 (and_27_out, d_ff_3_q[2], d_ff_3_q[1], ~d_ff_3_q[0]);  // AND_Gate
  and and_28 (and_28_out, p2_prime_p1p0_prime, or_4_out);
  or or_4 (or_4_out, score, and_13_out);
  and and_29 (and_29_out, or_5_out, and_1_out);
  or or_5 (or_5_out, and_15_out, and_14_out);
  not not_8 (not_8_out, d_ff_3_q[1]);
  // AND_Gate and_30 has open pins: in0=d_ff_3_q[2], in1=not_8_out, in2=not_7_out, in3=or_1_out, out=open
  not not_9 (not_9_out, d_ff_3_q[1]);
  not not_10 (not_10_out, d_ff_3_q[0]);
  or or_6 (or_6_out, and_2_out, and_22_out, and_19_out, and_20_out, and_21_out, and_23_out);
  or or_7 (or_7_out, and_25_out, and_24_out, and_6_out, and_8_out, and_9_out, and_10_out, and_26_out, and_11_out, and_31_out);
  and and_31 (and_31_out, and_27_out, score);
  or or_8 (or_8_out, and_27_out, and_11_out, and_12_out, and_28_out, and_29_out, and_32_out);
  and and_32 (and_32_out, ~d_ff_3_q[2], d_ff_3_q[1], not_7_out, ~byP2, xEnd);  // AND_Gate
  Decoder #(.select(3), .enable("false")) decoder_1 (
    .out0(state0), .out1(state1), .out2(state2), .out3(state3), .out4(state4), .out5(state5), .out6(state6),
    .out7(state7), .sel(d_ff_3_q));
  D_Flip_Flop d_ff_1 (.clk(clock_out), .D(or_6_out), .Q(d_ff_3_q[2]));  // open: Qn, preset, en, reset
  D_Flip_Flop d_ff_2 (.clk(clock_out), .D(or_7_out), .Q(d_ff_3_q[1]));  // open: Qn, preset, en, reset
  D_Flip_Flop d_ff_3 (.clk(clock_out), .D(or_8_out), .Q(d_ff_3_q[0]));  // open: Qn, preset, en, reset
  or or_9 (state2_3, state2, state3);
  nor nor_1 (scoreStop, state4, state5);
  Clock clock (.out(clock_out));
  or or_10 (or_10_out, state7, state0);
  Multiplexer multiplexer_1 (.in0(1'b1), .in1(Win), .out(multiplexer_1_out), .sel(or_10_out));  // open: en
  LED led_1 (.in(or_11_out));
  or or_11 (or_11_out, comparator_3_eq, state4);
  or or_12 (score, comparator_4_eq, comparator_3_eq);
  Counter #(.width(4), .max('hf)) counter_1 (
    .Q(counter_1_q), .clk(state4), .clr(state7));  // open: load, D, count, carry
  not not_11 (byP1, or_13_out);
  or or_13 (or_13_out, and_33_out[9], and_33_out[8], and_33_out[7], and_33_out[6], and_33_out[5], and_33_out[3], and_33_out[2], and_33_out[1], and_33_out[0], and_33_out[4]);
  assign and_33_out = demultiplexer_1_out1 & player1_1_outplayer1;  // AND_Gate and_33, 10 bits wide
  Comparator #(.width(5), .mode("unsigned")) comparator_1 (
    .a(5'b00001), .b(register_1_q), .eq(xBegin), .lt(comparator_1_lt));  // open: gt
  not not_12 (not_12_out, comparator_1_lt);
  Comparator #(.width(5), .mode("unsigned")) comparator_2 (
    .a(register_1_q), .b(5'b10010), .eq(xEnd), .lt(loop1));  // open: gt
  Comparator #(.width(4), .mode("unsigned")) comparator_3 (
    .a(4'b1010), .b(counter_1_q), .eq(comparator_3_eq));  // open: gt, lt
  // Probe on demultiplexer_1_out1
  Counter #(.width(1), .max('h1)) counter_2 (
    .D(xor_1_out), .Q(counter_2_q), .clk(xor_1_out), .clr(state6));  // open: load, count, carry
  xor xor_1 (xor_1_out, not_12_out, xEnd);
  and and_34 (and_34_out, multiplexer_1_out, clock_out);
  LED led_2 (.in(or_14_out));
  Counter #(.width(4), .max('ha)) counter_3 (
    .Q(counter_3_q), .clk(state5), .clr(state7));  // open: load, D, count, carry
  or or_14 (or_14_out, comparator_4_eq, state5);
  not not_13 (byP2, or_15_out);
  or or_15 (or_15_out, and_35_out[9], and_35_out[8], and_35_out[7], and_35_out[6], and_35_out[5], and_35_out[3], and_35_out[2], and_35_out[1], and_35_out[0], and_35_out[4]);
  assign and_35_out = demultiplexer_1_out18 & or_17_out;  // AND_Gate and_35, 10 bits wide
  and and_36 (and_36_out, ~state4, counter_2_q);  // AND_Gate
  and and_37 (and_37_out, and_34_out, ~state4);  // AND_Gate
  // OR_Gate or_16 has open pins: in0=state2_3, in1=state1, out=open
  Comparator #(.width(4), .mode("unsigned")) comparator_4 (
    .a(4'b1010), .b(counter_3_q), .eq(comparator_4_eq));  // open: gt, lt
  // Probe on player1_1_outplayer1
  Counter #(.width(5), .max('h13), .ongoal("load")) countBall_X (
    .load(and_36_out), .Q(countBall_X_q), .clk(and_37_out), .clr(state4));  // open: D, count, carry
  Counter #(.width(4), .max('h9), .ongoal("load")) countBall_Y (
    .D(4'b0001), .Q(countBall_Y_q), .clk(and_34_out));  // open: load, count, carry, clr
  // Probe on joystick_1_x
  Joystick joystick_1 (.x(joystick_1_x), .y(joystick_1_y));
  // Probe on joystick_1_y
  DotMatrix #(.matrixcols(20), .matrixrows(10)) dotmatrix_1 (
    .col0(player1_1_outplayer1), .col1(demultiplexer_1_out1), .col2(demultiplexer_1_out2),
    .col3(demultiplexer_1_out3), .col4(demultiplexer_1_out4), .col5(demultiplexer_1_out5),
    .col6(demultiplexer_1_out6), .col7(demultiplexer_1_out7), .col8(demultiplexer_1_out8),
    .col9(demultiplexer_1_out9), .col10(demultiplexer_1_out10), .col11(demultiplexer_1_out11),
    .col12(demultiplexer_1_out12), .col13(demultiplexer_1_out13), .col14(demultiplexer_1_out14),
    .col15(demultiplexer_1_out15), .col16(demultiplexer_1_out16), .col17(demultiplexer_1_out17),
    .col18(demultiplexer_1_out18), .col19(or_17_out));
  player1 player1_1 (.OutPlayer1(player1_1_outplayer1), .in(joystick_1_y));
  Register #(.width(5), .trigger("high")) register_1 (
    .D(countBall_X_q), .en(and_37_out), .Q(register_1_q), .clk(and_37_out));  // open: clr
  Multiplexer #(.width(4), .enable("false")) multiplexer_2 (.in1(4'b0101), .sel(state0));  // open: in0, out
  _7_Segment_Display u_7_segment_display_1 ();  // open: g, f, a, b, e, d, c, dp
  Comparator #(.width(10), .mode("unsigned")) comparator_5 (
    .a(10'h1), .b(multiplexer_4_out), .eq(yBegin), .lt(comparator_5_lt));  // open: gt
  not not_14 (not_14_out, comparator_5_lt);
  Comparator #(.width(10), .mode("unsigned")) comparator_6 (
    .a(multiplexer_4_out), .b(10'h200), .eq(yEnd));  // open: gt, lt
  _7_Segment_Display u_7_segment_display_2 ();  // open: g, f, a, b, e, d, c, dp
  Demultiplexer #(.select(5), .width(10), .enable("false")) demultiplexer_1 (
    .out1(demultiplexer_1_out1), .out2(demultiplexer_1_out2), .out3(demultiplexer_1_out3),
    .out4(demultiplexer_1_out4), .out5(demultiplexer_1_out5), .out6(demultiplexer_1_out6),
    .out7(demultiplexer_1_out7), .out8(demultiplexer_1_out8), .out9(demultiplexer_1_out9),
    .out10(demultiplexer_1_out10), .out11(demultiplexer_1_out11), .out12(demultiplexer_1_out12),
    .out13(demultiplexer_1_out13), .out14(demultiplexer_1_out14), .out15(demultiplexer_1_out15),
    .out16(demultiplexer_1_out16), .out17(demultiplexer_1_out17), .out18(demultiplexer_1_out18),
    .out19(demultiplexer_1_out19), .in(multiplexer_4_out), .sel(register_1_q));  // open: out0, out20, out21, out22, out23, out24, out25, out26, out27, out28, out29, out30, out31
  Counter #(.width(1), .max('h1)) counter_4 (
    .D(xor_2_out), .Q(counter_4_q), .clk(xor_2_out));  // open: load, count, carry, clr
  xor xor_2 (xor_2_out, not_14_out, yEnd);
  Shifter #(.width(10)) shifter_1 (.in(10'h1), .\dist (countBall_Y_q), .out(shifter_1_out));
  Shifter #(.width(10), .shift("lr")) shifter_2 (.in(10'h200), .\dist (countBall_Y_q), .out(shifter_2_out));
  // Probe on joystick_2_x
  Joystick joystick_2 (.x(joystick_2_x), .y(joystick_2_y));
  // Probe on joystick_2_y
  player2 player2_1 (.OutPlayer2(player2_1_outplayer2), .inp(joystick_2_y));
  assign or_17_out = demultiplexer_1_out19 | player2_1_outplayer2;  // OR_Gate or_17, 10 bits wide
  not not_15 (by, counter_4_q);
  Multiplexer #(.width(10), .enable("false")) multiplexer_3 (
    .in0(shifter_1_out), .in1(shifter_2_out), .out(multiplexer_3_out), .sel(counter_4_q));
  Register #(.width(10)) ball_Y (.D(multiplexer_3_out), .en(and_34_out), .Q(ball_Y_q), .clk(and_34_out));  // open: clr
  // OR_Gate or_18 has open pins: in0=state1, in1=state2_3, out=open
  Register #(.width(10)) ball_Y_2 (.D(ball_Y_q), .Q(ball_Y_2_q), .clk(and_34_out));  // open: en, clr
  Multiplexer #(.width(10), .enable("false")) multiplexer_4 (
    .in0(ball_Y_q), .in1(ball_Y_2_q), .out(multiplexer_4_out), .sel(state4));

  // Notes on the sheet:
  //   P2
  //   P1
  //   P0
  //   reset
  //   N2
  //   N1
  //   N0
  //   GTU Ping Pong Game - 2019
  //   player2_Score
  //   ball_Y != P1
  //   reset
  //   go
  //   player1_Score
  //   ball_Y != P2
  //   shift_X
  //   clearCountX
  //   clearCountY
  //   random
  //   0000000001
  //   shift_up
  //   1000000000
  //   shift_bottom
  //   ball_Y1
  //   shift_Y
endmodule

module player1 (
  input  [3:0] in,
  output [9:0] OutPlayer1
);

  wire and_1_out, and_2_out, and_3_out, clock_1_out, comparator_2_lt, comparator_3_gt, d_ff_1_q, not_1_out,
       not_2_out, not_3_out;
  wire [0:0] comparator_1_gt, comparator_1_lt;
  wire [9:0] multiplexer_1_out, multiplexer_2_out, multiplexer_3_out, shifter_1_out, shifter_2_out;

  Clock clock_1 (.out(clock_1_out));
  // Probe on multiplexer_2_out
  Comparator #(.width(1)) comparator_1 (
    .a(and_1_out), .b(and_2_out), .gt(comparator_1_gt[0]), .lt(comparator_1_lt[0]));  // open: eq
  Multiplexer #(.width(10), .enable("false")) multiplexer_1 (
    .in0(multiplexer_2_out), .in1(OutPlayer1), .out(multiplexer_1_out), .sel(comparator_1_lt[0]));
  D_Flip_Flop d_ff_1 (.clk(clock_1_out), .D(clock_1_out), .Q(d_ff_1_q));  // open: Qn, preset, en, reset
  and and_1 (and_1_out, in[0], in[1], in[2], in[3]);
  and and_2 (and_2_out, in[0], not_1_out, not_2_out, not_3_out);
  Shifter #(.width(10), .shift("lr")) shifter_1 (
    .in(multiplexer_1_out), .\dist ({3'b000, comparator_1_lt[0]}), .out(shifter_1_out));
  // Probe on 10'h7
  // Probe on 10'h380
  Multiplexer #(.width(10), .enable("false")) multiplexer_2 (
    .in0(10'hf), .in1(OutPlayer1), .out(multiplexer_2_out), .sel(d_ff_1_q));
  Shifter #(.width(10)) shifter_2 (.in(multiplexer_2_out), .\dist ({3'b000, comparator_1_gt[0]}), .out(shifter_2_out));
  not not_1 (not_1_out, in[1]);
  not not_2 (not_2_out, in[2]);
  not not_3 (not_3_out, in[3]);
  Comparator #(.width(10)) comparator_2 (.a(10'h7), .b(shifter_1_out), .lt(comparator_2_lt));  // open: gt, eq
  Comparator #(.width(10)) comparator_3 (.a(shifter_2_out), .b(10'h380), .gt(comparator_3_gt));  // open: eq, lt
  Multiplexer #(.width(10), .enable("false")) multiplexer_3 (
    .in0(shifter_1_out), .in1(shifter_2_out), .out(multiplexer_3_out), .sel(comparator_1_gt[0]));
  and and_3 (and_3_out, comparator_2_lt, comparator_3_gt);
  Register #(.width(10)) register_1 (
    .D(multiplexer_3_out), .en(and_3_out), .Q(OutPlayer1), .clk(clock_1_out));  // open: clr

  // Notes on the sheet:
  //   0001111100
  //   shift_right
  //   shift_left
endmodule

module player2 (
  input  [3:0] inp,
  output [9:0] OutPlayer2
);

  wire and_1_out, and_2_out, and_3_out, clock_1_out, comparator_2_lt, comparator_3_gt, d_ff_1_q, not_1_out,
       not_2_out, not_3_out;
  wire [0:0] comparator_1_gt, comparator_1_lt;
  wire [9:0] multiplexer_1_out, multiplexer_2_out, multiplexer_3_out, shifter_1_out, shifter_2_out;

  Clock clock_1 (.out(clock_1_out));
  // Probe on multiplexer_2_out
  Comparator #(.width(1)) comparator_1 (
    .a(and_1_out), .b(and_2_out), .gt(comparator_1_gt[0]), .lt(comparator_1_lt[0]));  // open: eq
  Multiplexer #(.width(10), .enable("false")) multiplexer_1 (
    .in0(multiplexer_2_out), .in1(OutPlayer2), .out(multiplexer_1_out), .sel(comparator_1_lt[0]));
  D_Flip_Flop d_ff_1 (.clk(clock_1_out), .D(clock_1_out), .Q(d_ff_1_q));  // open: Qn, preset, en, reset
  and and_1 (and_1_out, inp[0], inp[1], inp[2], inp[3]);
  and and_2 (and_2_out, inp[0], not_1_out, not_2_out, not_3_out);
  Shifter #(.width(10), .shift("lr")) shifter_1 (
    .in(multiplexer_1_out), .\dist ({3'b000, comparator_1_lt[0]}), .out(shifter_1_out));
  // Probe on 10'h7
  // Probe on 10'h380
  Multiplexer #(.width(10), .enable("false")) multiplexer_2 (
    .in0(10'h3c), .in1(OutPlayer2), .out(multiplexer_2_out), .sel(d_ff_1_q));
  Shifter #(.width(10)) shifter_2 (.in(multiplexer_2_out), .\dist ({3'b000, comparator_1_gt[0]}), .out(shifter_2_out));
  not not_1 (not_1_out, inp[1]);
  not not_2 (not_2_out, inp[2]);
  not not_3 (not_3_out, inp[3]);
  Comparator #(.width(10)) comparator_2 (.a(10'h7), .b(shifter_1_out), .lt(comparator_2_lt));  // open: gt, eq
  Comparator #(.width(10)) comparator_3 (.a(shifter_2_out), .b(10'h380), .gt(comparator_3_gt));  // open: eq, lt
  Multiplexer #(.width(10), .enable("false")) multiplexer_3 (
    .in0(shifter_1_out), .in1(shifter_2_out), .out(multiplexer_3_out), .sel(comparator_1_gt[0]));
  and and_3 (and_3_out, comparator_2_lt, comparator_3_gt);
  Register #(.width(10)) register_1 (
    .D(multiplexer_3_out), .en(and_3_out), .Q(OutPlayer2), .clk(clock_1_out));  // open: clr

  // Notes on the sheet:
  //   0001111100
  //   shift_right
  //   shift_left
endmodule
